# Fritzing sketch Pieces_TCC (saved by Fritzing 0.9.3b)
breadboards: 1

parts:
  LCD1 = LCD screen  # not connected
  Mod1 = sensor_biometrico
  Componente2 = Arduino Uno (Rev3)
  LCM1602_IIC1 = LCM1602 IIC [part_number="LCM1602 IIC" chip_label="LCM1602 IIC" package="DIP (Dual Inline) [THT]"]
  R1 = Resistor [tolerance=±5% resistance=560 package="1206 [SMD]"]
  R2 = Resistor [tolerance=±5% resistance=330 package="1206 [SMD]"]
  R3 = Resistor [tolerance=±5% resistance=220 package="1206 [SMD]"]
  U1 = SWITCH_SPDT [package=kps-1290]
  U2 = SWITCH_SPDT [package=kps-1290]
  LED1 = LED - 3mm [color="Yellow (595nm)" package="3 mm [THT]"]
  X2 = USB Connectors [package=usb-microb]
  J1 = Basic Servo
  Gizwits_WiFi_Witty_ESP-12F1 = Gizwits WiFi Witty ESP-12F  # not connected

nets:
  VCC: Mod1.VCC, Componente2.3V3
  N1: Mod1.TX, U2.S
  N2: Mod1.RX, R1.Pin_0, R2.Pin_1
  GND: Mod1.GND, Componente2.GND, LCM1602_IIC1.GND, R1.Pin_1, R3.Pin_0, X2.GND, J1.gnd
  N3: Componente2.A4/SDA, LCM1602_IIC1.SCL
  N4: Componente2.A5/SCL, LCM1602_IIC1.SDA
  N5: Componente2.D8, J1.pulse
  N6: Componente2.D0/RX, U2.P
  N7: Componente2.D1/TX, U1.P
  N8: Componente2.D4, LED1.anode
  5V: Componente2.5V, LCM1602_IIC1.VCC
  N9: R2.Pin_0, U1.S
  N10: R3.Pin_1, LED1.cathode

custom parts:
  sensor_biometrico: Adafruit Optical Fingerprint Sensor
  LCM1602 IIC: I2C-Module to use a 1602 or 2004 LCD on with the wire.h libory Serial LCD Modul
